# Fritzing sketch servo (saved by Fritzing 0.9.3b)
breadboards: 1

parts:
  パーツ1 = Arduino Uno (Rev3)
  J1 = Basic Servo
  VCC1 = Battery block 9V

nets:
  N1: パーツ1.D9_PWM, J1.pulse
  N2: J1.gnd, VCC1.-
  N3: J1.vcc, VCC1.+
